# Fritzing sketch BLINK_TIP122 (saved by Fritzing 0.9.9b)
breadboards: 1

parts:
  Teensy1 = Teensy 3.0  # not connected
  LED1 = smd LED [color="Red (633nm)" package="1206 [SMD]"]
  R1 = Resistor [tolerance=±1% resistance=4.7k package=THT]
  Q1 = npn-Powertransistor [part_number=TIP122 package="TO220 [THT]"]
  R2 = Resistor [tolerance=±1% resistance=1.5 package=THT]
  Power_plug1 = Power plug [part_number="12V DC"]

nets:
  N1: LED1.cathode, Q1.collector
  N2: LED1.anode, R1.Pin_1
  N3: R1.Pin_0, Power_plug1.VCC
  N4: Q1.base, R2.Pin_1
  N5: Q1.emitter, Power_plug1.GND
