# Fritzing sketch BLINK_TIP122_VALVE (saved by Fritzing 0.9.9b)
breadboards: 1

parts:
  Teensy1 = Teensy 3.0  # not connected
  Q1 = npn-Powertransistor [part_number=TIP122 package="TO220 [THT]"]
  R2 = Resistor [tolerance=±1% resistance=1.5 package=THT]
  Power_plug1 = Power plug [part_number="12V DC"]
  J1 = Screw terminal - 2 pins [package=THT]
  L1 = Solenoid
  D1 = Rectifier Diode [part_number=1N4001 package="Melf DO-213 AA [SMD]"]  # not connected

nets:
  N1: Q1.base, R2.Pin_1
  N2: Q1.collector, J1.pin1, L1.pin1
  N3: Q1.emitter, Power_plug1.GND
  N4: Power_plug1.VCC, J1.pin2, L1.pin2
